// Logisim project Labo_execute1_2.circ as structural Verilog: 22 circuits, main circuit main
module main (
);

  wire mainclk, reset_out, Sys_clk;
  wire [0:0] prodis1_1_inst_adr;
  wire [3:0] IRQ1_out;
  wire [14:0] prodis1_1_inst_adr_2;
  wire [15:0] rom_1_data;

  // Text text_1: pin names not known
  // Text text_2: pin names not known
  // Text text_3: pin names not known
  // Text text_4: pin names not known
  // Text text_5: pin names not known
  Button IRQ1 (.out(IRQ1_out[0]));
  Button IRQ2 (.out(IRQ1_out[1]));
  Button IRQ3 (.out(IRQ1_out[2]));
  Button IRQ4 (.out(IRQ1_out[3]));
  Button reset (.out(reset_out));
  Clock #(.highDuration(4), .lowDuration(4)) clk (.out(mainclk));
  Clock sysclk (.out(Sys_clk));
  ROM #(.addrWidth(15), .dataWidth(16)) rom_1 (.addr(prodis1_1_inst_adr_2), .data(rom_1_data));
  prodis1 prodis1_1 (
    .inst_adr({prodis1_1_inst_adr_2, prodis1_1_inst_adr[0]}), .inst_data(rom_1_data), .reset(reset_out),
    .interrupt(IRQ1_out), .clock(mainclk));  // open: out_6

  // Notes on the sheet:
  //   Ne pas changer le nom des clocks
  //   contents of rom_1 (hex, n*v repeats v):
  //   2003 1c02 1dd3 181c 4023 a1 1a58
endmodule

module prodis1 (
  input  [15:0] inst_data,
  input  [3:0] interrupt,
  input  reset,
  input  clock,
  output [15:0] inst_adr,
  output [15:0] out_6
);

  wire branch, interrupt_en, link_en;
  wire [2:0] decode_1_adr_reg_d, decode_1_adr_reg_m, decode_1_adr_reg_n, decode_1_imm3, reg_bank_control_bus;
  wire [3:0] mem_control_bus;
  wire [4:0] decode_1_imm5;
  wire [5:0] fetch_control_bus;
  wire [7:0] decode_1_offset_cond_or_imm8;
  wire [15:0] bank_register_1_reg_data_m_out, bank_register_1_reg_data_n_out, fetch_1_inst_out, PC_fut,
       PC_pres;
  wire [22:0] decode_1_execute_control_bus;

  // Text text_1: pin names not known
  // Text text_2: pin names not known
  // Text text_3: pin names not known
  // Text text_4: pin names not known
  // Text text_5: pin names not known
  Fetch fetch_1 (
    .jump_adr({16{1'b0}}), .inst_out(fetch_1_inst_out), .inst_data(inst_data), .inst_adr(inst_adr),
    .cpsr({5{1'b0}}), .sel_PC(fetch_control_bus), .IRQ_bus(interrupt), .PC_fut(PC_fut), .PC_pres(PC_pres),
    .interrupt_en(interrupt_en), .branch(branch), .clock(clock), .reset(reset));
  // Probe on out_6
  // Probe on fetch_1_inst_out
  Decode decode_1 (
    .instruction(fetch_1_inst_out), .adr_reg_m(decode_1_adr_reg_m), .imm3(decode_1_imm3),
    .adr_reg_n(decode_1_adr_reg_n), .adr_reg_d(decode_1_adr_reg_d), .imm5(decode_1_imm5),
    .offset_cond_or_imm8(decode_1_offset_cond_or_imm8), .execute_control_bus(decode_1_execute_control_bus),
    .mem_control_bus(mem_control_bus), .reg_bank_control_bus(reg_bank_control_bus),
    .fetch_control_bus(fetch_control_bus), .link_en(link_en));  // open: offset_incond
  Bank_Register bank_register_1 (
    .reg_sel_n(decode_1_adr_reg_n), .reg_data_n_out(bank_register_1_reg_data_n_out), .reg_data_in(out_6),
    .reg_sel_wr(decode_1_adr_reg_d), .reg_sel_m(decode_1_adr_reg_m),
    .reg_data_m_out(bank_register_1_reg_data_m_out), .interupt_en(interrupt_en),
    .reg_sel_mem_data(decode_1_adr_reg_d), .PC_fut(PC_fut), .PC_pres(PC_pres), .clock(clock), .reset(reset),
    .br_control_bus(reg_bank_control_bus), .branch(branch), .link_en(link_en));  // open: reg_mem_data_out
  // Probe on decode_1_imm5
  EXECUTE execute_1 (
    .reg_data_out_n(bank_register_1_reg_data_n_out), .reg_data_out_m(bank_register_1_reg_data_m_out),
    .imm3(decode_1_imm3), .offset_cond_or_imm8(decode_1_offset_cond_or_imm8),
    .execute_control_bus(decode_1_execute_control_bus), .imm5(decode_1_imm5), .OUT_EXECUTE(out_6));

  // Other names for the same wires on the sheet: CLK = clock; RST = reset

  // Notes on the sheet:
  //   HEIG-VD - Institut ReDS
  //   Auteur:
  //   Date: 05.03.14
  //   LABO ARO 2 - EXECUTE
  //   WRITE BACK : Retour de la donnée dans la banque des registres
endmodule

module Fetch (
  input  [15:0] PC_pres,
  input  [15:0] inst_data,
  input  [15:0] jump_adr,
  input  [3:0] IRQ_bus,
  input  reset,
  input  [5:0] sel_PC,
  input  clock,
  input  [4:0] cpsr,
  output [15:0] inst_adr,
  output [15:0] inst_out,
  output [15:0] PC_fut,
  output interrupt_en,
  output branch
);

  wire test_cond_1_test_cond;
  wire [15:0] adder_1_out, interrupt_adr;

  // Text text_1: pin names not known
  // Text text_2: pin names not known
  // Text text_3: pin names not known
  // Text text_4: pin names not known
  // Text text_5: pin names not known
  Test_cond test_cond_1 (
    .cond(sel_PC[5:2]), .Z(cpsr[0]), .C(cpsr[2]), .N(cpsr[1]), .V(cpsr[3]),
    .test_cond(test_cond_1_test_cond), .cond_en(sel_PC[1]));
  Adder #(.width(16)) adder_1 (.a(PC_pres), .b(16'h2), .out(adder_1_out));  // open: cin, cout
  and and_1 (branch, sel_PC[0], test_cond_1_test_cond);
  Multiplexer #(.select(2), .width(16), .enable("false")) multiplexer_1 (
    .in0(adder_1_out), .in1(jump_adr), .in2(interrupt_adr), .in3(interrupt_adr), .out(PC_fut),
    .sel({interrupt_en, branch}));
  Gestion_Interruption gestion_interruption_1 (
    .IRQ4(IRQ_bus[3]), .IRQ3(IRQ_bus[2]), .interrupt_en(interrupt_en), .IRQ2(IRQ_bus[1]), .IRQ1(IRQ_bus[0]),
    .clock(clock), .I_flag(cpsr[4]), .interrupt_adr(interrupt_adr), .reset(reset));

  assign inst_adr = PC_pres;
  assign inst_out = inst_data;

  // Other names for the same wires on the sheet: I_flag = cpsr[4]

  // Notes on the sheet:
  //   FETCH v1.1
  //   la valeur actuelle du PC, soit en sélectionnant une adresse de saut.
  //   Ce bloc test si la condition requise par l'instruction est correcte.
  //   Cela n'est utile que pour les branch en Thumb code.
  //   Ce bloc s'occupe d'envoyer la bonne adresse à la mémoire d'instruction, soit en incrémentant
  //   Le bloc reçoit en retour l'instruction stockée dans la mémoire, qu'il va en ensuite envoyer au bloc suivant : Le décodage.
  //   Incrémentation du PC 
endmodule

module Test_cond (
  input  cond_en,
  input  [3:0] cond,
  input  Z,
  input  C,
  input  N,
  input  V,
  output test_cond
);

  wire and_1_out, and_2_out, comparator_1_eq, not_1_out, not_2_out, not_3_out, not_4_out, not_5_out,
       not_6_out, not_7_out, not_8_out, or_1_out, or_2_out;
  wire [3:0] multiplexer_1_out;

  // Text text_1: pin names not known
  // Text text_2: pin names not known
  // Text text_3: pin names not known
  // Text text_4: pin names not known
  // Text text_5: pin names not known
  and and_1 (and_1_out, C, not_1_out);
  not not_1 (not_1_out, Z);
  not not_2 (not_2_out, C);
  or or_1 (or_1_out, not_2_out, Z);
  Comparator #(.width(1), .mode("unsigned")) comparator_1 (.a(N), .b(V), .eq(comparator_1_eq));  // open: gt, lt
  not not_3 (not_3_out, Z);
  not not_4 (not_4_out, comparator_1_eq);
  and and_2 (and_2_out, comparator_1_eq, not_3_out);
  or or_2 (or_2_out, not_4_out, Z);
  not not_5 (not_5_out, Z);
  not not_6 (not_6_out, C);
  not not_7 (not_7_out, N);
  not not_8 (not_8_out, V);
  Multiplexer #(.width(4), .enable("false")) multiplexer_1 (
    .in0(4'b1110), .in1(cond), .out(multiplexer_1_out), .sel(cond_en));
  Multiplexer #(.select(4), .enable("false")) multiplexer_2 (
    .in0(Z), .in1(not_5_out), .in2(C), .in3(not_6_out), .in4(N), .in5(not_7_out), .in6(V), .in7(not_8_out),
    .in8(and_1_out), .in9(or_1_out), .in10(comparator_1_eq), .in11(not_4_out), .in12(and_2_out),
    .in13(or_2_out), .in14(1'b1), .in15(1'b1), .out(test_cond), .sel(multiplexer_1_out));

  // Notes on the sheet:
  //   TEST COND v1.0
  //   sélectionnera le bon test.
  //   Ce bloc reçoit les valeurs actuels des flags de conditions, et, suivant l'instruction conditionnelle,
  //   Si l'instruction n'est pas conditionnelle, alors on choisis la "condition" always, qui est toujours à 1.
  //   Always (Inconditionnel)
endmodule

module Gestion_Interruption (
  input  IRQ4,
  input  IRQ3,
  input  IRQ2,
  input  IRQ1,
  input  clock,
  input  I_flag,
  input  reset,
  output interrupt_en,
  output [15:0] interrupt_adr
);

  wire rst, s_r_ff_1_q, s_r_ff_2_q, s_r_ff_3_q, s_r_ff_4_q;
  wire [1:0] priority_encoder_1_out;

  // Text text_1: pin names not known
  // Text text_2: pin names not known
  // Text text_3: pin names not known
  // Text text_4: pin names not known
  // Text text_5: pin names not known
  S_R_Flip_Flop s_r_ff_1 (.S(IRQ4), .R(1'b0), .clk(clock), .Q(s_r_ff_1_q), .reset(rst));  // open: Qn, preset
  S_R_Flip_Flop s_r_ff_2 (.S(IRQ3), .R(1'b0), .clk(clock), .Q(s_r_ff_2_q), .reset(rst));  // open: Qn, preset
  S_R_Flip_Flop s_r_ff_3 (.S(IRQ2), .R(1'b0), .clk(clock), .Q(s_r_ff_3_q), .reset(rst));  // open: Qn, preset
  S_R_Flip_Flop s_r_ff_4 (.S(IRQ1), .R(1'b0), .clk(clock), .Q(s_r_ff_4_q), .reset(rst));  // open: Qn, preset
  or or_1 (rst, I_flag, reset);
  Priority_Encoder #(.select(2)) priority_encoder_1 (
    .in0(s_r_ff_4_q), .in1(s_r_ff_3_q), .in2(s_r_ff_2_q), .in3(s_r_ff_1_q), .out(priority_encoder_1_out));  // open: gs, en_out, en_in
  or or_2 (interrupt_en, s_r_ff_1_q, s_r_ff_2_q, s_r_ff_3_q, s_r_ff_4_q);
  Multiplexer #(.select(2), .width(16), .enable("false")) multiplexer_1 (
    .in0(16'he000), .in1(16'he200), .in2(16'he400), .in3(16'he600), .out(interrupt_adr),
    .sel(priority_encoder_1_out));

  // Other names for the same wires on the sheet: clk = clock

  // Notes on the sheet:
  //   INTERRUPT UNIT v1.0
  //   4 interruptions sont pour l'instant en place. Les sauts vont aux adresses suivantes en fonction de l'IRQ :
  //   IRQ 1 : 0xE000
  //   IRQ 2 : 0xE200
  //   IRQ 3 : 0xE400
  //   IRQ 4 : 0xE600
endmodule

module Bank_Register (
  input  [2:0] reg_sel_n,
  input  [15:0] reg_data_in,
  input  [2:0] reg_sel_wr,
  input  [2:0] reg_sel_m,
  input  interupt_en,
  input  link_en,
  input  branch,
  input  [2:0] reg_sel_mem_data,
  input  [15:0] PC_fut,
  input  clock,
  input  reset,
  input  [2:0] br_control_bus,
  output [15:0] reg_data_n_out,
  output [15:0] reg_data_m_out,
  output [15:0] reg_mem_data_out,
  output [15:0] PC_pres
);

  wire decoder_1_out0, decoder_1_out1, decoder_1_out2, decoder_1_out3, decoder_1_out4, decoder_1_out5,
       decoder_1_out6, decoder_1_out7, not_1_out, pc_lr_1_lr_en;
  wire [15:0] LR_q, multiplexer_1_out, pc_lr_1_lr_in, Reg0_q, Reg1_q, Reg2_q, Reg3_q, Reg4_q, SP_q;

  // Text text_1: pin names not known
  // Text text_2: pin names not known
  // Text text_3: pin names not known
  // Text text_4: pin names not known
  // Text text_5: pin names not known
  Decoder #(.select(3)) decoder_1 (
    .out0(decoder_1_out0), .out1(decoder_1_out1), .out2(decoder_1_out2), .out3(decoder_1_out3),
    .out4(decoder_1_out4), .out5(decoder_1_out5), .out6(decoder_1_out6), .out7(decoder_1_out7),
    .sel(reg_sel_wr), .en(br_control_bus[2]));
  not not_1 (not_1_out, decoder_1_out7);
  Multiplexer #(.width(16), .enable("false")) multiplexer_1 (
    .in0(reg_data_in), .in1(PC_fut), .out(multiplexer_1_out), .sel(not_1_out));
  PC_LR pc_lr_1 (
    .data_in(reg_data_in), .pc(PC_pres), .sel_reg(decoder_1_out6), .interrupt_en(interupt_en),
    .LR_in(pc_lr_1_lr_in), .LR_en(pc_lr_1_lr_en), .branch(branch), .link_en(link_en));
  Register #(.width(16)) Reg0 (.D(reg_data_in), .en(decoder_1_out0), .clk(clock), .Q(Reg0_q), .clr(reset));
  Register #(.width(16)) Reg1 (.D(reg_data_in), .en(decoder_1_out1), .clk(clock), .Q(Reg1_q), .clr(reset));
  Register #(.width(16)) Reg2 (.D(reg_data_in), .en(decoder_1_out2), .clk(clock), .Q(Reg2_q), .clr(reset));
  Register #(.width(16)) Reg3 (.D(reg_data_in), .en(decoder_1_out3), .clk(clock), .Q(Reg3_q), .clr(reset));
  Register #(.width(16)) Reg4 (.D(reg_data_in), .en(decoder_1_out4), .clk(clock), .Q(Reg4_q), .clr(reset));
  Register #(.width(16)) SP (.D(reg_data_in), .en(decoder_1_out5), .clk(clock), .Q(SP_q), .clr(reset));
  Register #(.width(16)) LR (.D(pc_lr_1_lr_in), .en(pc_lr_1_lr_en), .clk(clock), .Q(LR_q), .clr(reset));
  Register #(.width(16)) PC (.D(multiplexer_1_out), .en(1'b1), .clk(clock), .Q(PC_pres), .clr(reset));
  Multiplexer #(.select(3), .width(16), .enable("false")) multiplexer_2 (
    .in0(Reg0_q), .in1(Reg1_q), .in2(Reg2_q), .in3(Reg3_q), .in4(Reg4_q), .in5(SP_q), .in6(LR_q),
    .in7(PC_pres), .out(reg_data_n_out), .sel(reg_sel_n));
  Multiplexer #(.select(3), .width(16), .enable("false")) multiplexer_3 (
    .in0(Reg0_q), .in1(Reg1_q), .in2(Reg2_q), .in3(Reg3_q), .in4(Reg4_q), .in5(SP_q), .in6(LR_q),
    .in7(PC_pres), .out(reg_data_m_out), .sel(reg_sel_m));
  Multiplexer #(.select(3), .width(16), .enable("false")) multiplexer_4 (
    .in0(Reg0_q), .in1(Reg1_q), .in2(Reg2_q), .in3(Reg3_q), .in4(Reg4_q), .in5(SP_q), .in6(LR_q),
    .in7(PC_pres), .out(reg_mem_data_out), .sel(reg_sel_mem_data));

  // Other names for the same wires on the sheet: reg_bank_en = br_control_bus[0]; reg_mem_data_en = br_control_bus[1];
  //   reg_bank_wr = br_control_bus[2]; clk = clock

  // Notes on the sheet:
  //   BANK REGISTER v1.1
  //   Ce bloc contient les registres de PRODIS1.
  //   2 en tant qu'operand, et 1 une valeur à écrire en mémoire.
  //   Il y a 3 registres en sortie, car certaines instructions peuvent avoir besoin de 3 :
  //   L'adresse des registres étant sur 3 bits dans le Thumb Code, 8 registres sont donc disponibles.
  //   d'où un registre supplémentaire ici.
  //   La donnée "reg_mem_data_out" est une donnée qui va être écrite en mémoire de donnée.
  //   Pour qu'elle arrive en même temps que les autres informations propre au stockage dans le bloc mémoire,
  //   il faut attendre un coup d'horloge supplémentaire pendant que les autres informations s'executent,
endmodule

module PC_LR (
  input  [15:0] data_in,
  input  [15:0] pc,
  input  branch,
  input  sel_reg,
  input  interrupt_en,
  input  link_en,
  output [15:0] LR_in,
  output LR_en
);

  wire and_1_out, or_1_out;
  wire [15:0] adder_1_out;

  // Text text_1: pin names not known
  // Text text_2: pin names not known
  // Text text_3: pin names not known
  // Text text_4: pin names not known
  // Text text_5: pin names not known
  Adder #(.width(16)) adder_1 (.a(pc), .b(16'h2), .out(adder_1_out));  // open: cin, cout
  or or_1 (or_1_out, interrupt_en, link_en);
  Multiplexer #(.width(16), .enable("false")) multiplexer_1 (
    .in0(data_in), .in1(adder_1_out), .out(LR_in), .sel(and_1_out));
  and and_1 (and_1_out, branch, or_1_out);
  or or_2 (LR_en, sel_reg, or_1_out);
endmodule

module Decode (
  input  [15:0] instruction,
  output [2:0] adr_reg_m,
  output [2:0] imm3,
  output [2:0] adr_reg_n,
  output [2:0] adr_reg_d,
  output [4:0] imm5,
  output [10:0] offset_incond,
  output [7:0] offset_cond_or_imm8,
  output [2:0] reg_bank_control_bus,
  output [22:0] execute_control_bus,
  output link_en,
  output [3:0] mem_control_bus,
  output [5:0] fetch_control_bus
);

  wire sel_rm;
  wire [1:0] sel_rn;
  wire [2:0] data_splitter_1_rd_2_0, data_splitter_1_rd_or_rn_10_8, data_splitter_1_rn_or_rm_5_3;

  // Text text_1: pin names not known
  // Text text_2: pin names not known
  // Text text_3: pin names not known
  // Text text_4: pin names not known
  // Text text_5: pin names not known
  Data_Splitter data_splitter_1 (
    .instruction(instruction), .Rm_or_imm3_8_6(imm3), .Rn_or_Rm_5_3(data_splitter_1_rn_or_rm_5_3),
    .Rd_2_0(data_splitter_1_rd_2_0), .Imm5_10_6(imm5), .offset_incond_10_0(offset_incond),
    .offset_cond_or_imm8_7_0(offset_cond_or_imm8), .cond_11_8(fetch_control_bus[5:2]),
    .Rd_or_Rn_10_8(data_splitter_1_rd_or_rn_10_8));
  Control_Unit control_unit_1 (
    .instruction(instruction), .sel_op_shift(execute_control_bus[2:0]), .sel_mem(mem_control_bus[0]),
    .sel_rm(sel_rm), .sel_op_alu(execute_control_bus[6:3]), .reg_bank_en(reg_bank_control_bus[0]),
    .sel_operand_2(execute_control_bus[8:7]), .str_data(mem_control_bus[1]),
    .reg_bank_wr(reg_bank_control_bus[2]), .reg_mem_data_en(reg_bank_control_bus[1]),
    .sel_PC(fetch_control_bus[0]), .sel_mult_2(execute_control_bus[13:11]),
    .sel_operand_1(execute_control_bus[10:9]), .flag_en(execute_control_bus[17:14]),
    .cond_en(fetch_control_bus[1]), .ldr_data(mem_control_bus[2]), .sel_carry(execute_control_bus[19:18]),
    .sel_rn(sel_rn), .sel_shift(execute_control_bus[20]), .shift_c_unaffected(execute_control_bus[21]),
    .sel_cpsr(execute_control_bus[22]), .\byte (mem_control_bus[3]), .link_en(link_en));
  Multiplexer #(.select(2), .width(3), .enable("false")) multiplexer_1 (
    .in0(data_splitter_1_rn_or_rm_5_3), .in1(data_splitter_1_rd_2_0), .in2(data_splitter_1_rd_or_rn_10_8),
    .in3(3'b111), .out(adr_reg_n), .sel(sel_rn));
  Multiplexer #(.width(3), .enable("false")) multiplexer_2 (
    .in0(data_splitter_1_rd_2_0), .in1(data_splitter_1_rd_or_rn_10_8), .out(adr_reg_d), .sel(sel_rn[1]));
  Multiplexer #(.width(3), .enable("false")) multiplexer_3 (
    .in0(imm3), .in1(data_splitter_1_rn_or_rm_5_3), .out(adr_reg_m), .sel(sel_rm));

  // Other names for the same wires on the sheet: cond[3:0] = fetch_control_bus[5:2]

  // Notes on the sheet:
  //   DECODE v1.1
  //   aux bons timings.
  //   Ce bloc permet de décoder l'instruction qu'on reçoit du FETCH.
  //   Il est divisé en 2 sous-blocs : Data Splitter et Control Unit.
  //   Control Unit permet de détecter quelle instruction est entrée et de générer les signaux de contrôles 
  //   Data Splitter s'occupe de récupérer les informations qui peuvent être sortie de l'instruction sans autres traitement.
  //   Rd peut être utilisé comme operand dans le cas de certaines instruction, d'où ce mux.
  //   Les signaux de contrôles ont été regroupé en bus qui sont attribués à chaque bloc.
  //   registre de destination.
  //   Si Rd se trouve aux bits 10 à 8 de l'instruction, c'est qu'il sera utilisé comme opérand et comme 
endmodule

module Data_Splitter (
  input  [15:0] instruction,
  output [2:0] Rd_2_0,
  output [2:0] Rn_or_Rm_5_3,
  output [2:0] Rm_or_imm3_8_6,
  output [2:0] Rd_or_Rn_10_8,
  output [4:0] Imm5_10_6,
  output [3:0] cond_11_8,
  output [10:0] offset_incond_10_0,
  output [7:0] offset_cond_or_imm8_7_0
);

  // Text text_1: pin names not known
  // Text text_2: pin names not known
  // Text text_3: pin names not known
  // Text text_4: pin names not known
  // Text text_5: pin names not known

  assign cond_11_8 = instruction[11:8];
  assign Imm5_10_6 = instruction[10:6];
  assign offset_cond_or_imm8_7_0 = instruction[7:0];
  assign offset_incond_10_0 = instruction[10:0];
  assign Rd_2_0 = instruction[2:0];
  assign Rd_or_Rn_10_8 = instruction[10:8];
  assign Rm_or_imm3_8_6 = instruction[8:6];
  assign Rn_or_Rm_5_3 = instruction[5:3];

  // Notes on the sheet:
  //   DATA SPLITTER v1.0
  //   Split les différentes informations disponible dans l'instruction même.
  //   Les 2 numéros à la fin des noms de signaux indiquent leur emplacement dans l'instruction.
endmodule

module Control_Unit (
  input  [15:0] instruction,
  output [1:0] sel_rn,
  output [2:0] sel_op_shift,
  output sel_mem,
  output reg_bank_wr,
  output sel_rm,
  output [3:0] sel_op_alu,
  output str_data,
  output sel_PC,
  output reg_bank_en,
  output [1:0] sel_operand_2,
  output ldr_data,
  output reg_mem_data_en,
  output cond_en,
  output \byte ,
  output [1:0] sel_operand_1,
  output [2:0] sel_mult_2,
  output link_en,
  output [1:0] sel_carry,
  output sel_shift,
  output [3:0] flag_en,
  output shift_c_unaffected,
  output sel_cpsr
);

  wire [15:0] decode_control_1_instruction_out, execute_control_1_instruction_out,
       memory_control_1_instruction_out;

  // Text text_1: pin names not known
  // Text text_2: pin names not known
  // Text text_3: pin names not known
  // Text text_4: pin names not known
  // Text text_5: pin names not known
  Decode_Control decode_control_1 (
    .instruction_in(instruction), .instruction_out(decode_control_1_instruction_out), .sel_rm(sel_rm),
    .reg_mem_data_en(reg_mem_data_en), .reg_bank_en(reg_bank_en), .sel_rn(sel_rn), .link_en(link_en));
  Execute_Control execute_control_1 (
    .instruction_in(decode_control_1_instruction_out), .instruction_out(execute_control_1_instruction_out),
    .flag_z_en(flag_en[0]), .sel_op_shift(sel_op_shift), .sel_op_alu(sel_op_alu),
    .sel_operand_2(sel_operand_2), .sel_operand_1(sel_operand_1), .sel_mult_2(sel_mult_2), .cond_en(cond_en),
    .sel_carry(sel_carry), .sel_shift(sel_shift), .flag_n_en(flag_en[1]), .flag_c_en(flag_en[2]),
    .flag_v_en(flag_en[3]), .cond_en_2(shift_c_unaffected), .sel_cpsr(sel_cpsr));
  Memory_Control memory_control_1 (
    .instruction_in(execute_control_1_instruction_out), .instruction_out(memory_control_1_instruction_out),
    .sel_mem(sel_mem), .ldr_data(ldr_data), .str_data(str_data), .\byte (\byte ));
  Writeback_Control writeback_control_1 (
    .instruction_in(memory_control_1_instruction_out), .reg_bank_wr(reg_bank_wr), .sel_PC(sel_PC));

  // Notes on the sheet:
  //   CONTROL UNIT v1.0
  //   Gère les signaux de contrôle en fonction de l'instruction en cours.
  //   L'instruction va elle-même être retardée avec des registres pour générer les signaux aux bons timing dans les blocs de traitement.
  //   Chaque sous-blocs détecte l'instruction en cours et génère la bonne logique aux signaux de contrôles en fonction de cette dernière.
endmodule

module Decode_Opcode (
  input  [15:0] instruction,
  output add_r_r_r,
  output cmn_r_r,
  output bic_r_r,
  output add_r_r_imm,
  output cmp_r_imm,
  output cpy_r_r,
  output cmp_r_r,
  output mov_r_imm,
  output mov_pc,
  output adc_r_r,
  output mul_r_r,
  output add_r_imm,
  output ror_r_r,
  output and_r_r,
  output asr_r_r,
  output tst_r_r,
  output asr_r_r_imm,
  output eor_r_r,
  output bl_msb,
  output lsl_r_r_imm,
  output lsl_r_r,
  output bl_lsb,
  output lsr_r_r_imm,
  output lsr_r_r,
  output bx,
  output sub_r_r_r,
  output mvn_r_r,
  output sub_r_r_imm,
  output neg_r_r,
  output ldrh_r_r_imm,
  output orr_r_r,
  output ldrh_r_r_r,
  output sbc_r_r,
  output strh_r_r_imm,
  output sub_r_imm,
  output strh_r_r_r,
  output ldrb_r_r_imm,
  output b_cond,
  output ldrb_r_r_r,
  output b_incond,
  output strb_r_r_imm,
  output strb_r_r_r
);

  wire and_1_out, comparator_3_eq, comparator_4_eq, comparator_5_eq;

  // Text text_1: pin names not known
  // Text text_2: pin names not known
  // Text text_3: pin names not known
  // Text text_4: pin names not known
  // Text text_5: pin names not known
  Comparator #(.width(7), .mode("unsigned")) comparator_1 (
    .a(instruction[15:9]), .b(7'b0001100), .eq(add_r_r_r));  // open: gt, lt
  Comparator #(.width(7), .mode("unsigned")) comparator_2 (
    .a(instruction[15:9]), .b(7'b0001110), .eq(add_r_r_imm));  // open: gt, lt
  Comparator #(.width(10), .mode("unsigned")) comparator_3 (
    .a(instruction[15:6]), .b(10'h70), .eq(comparator_3_eq));  // open: gt, lt
  and and_1 (and_1_out, comparator_3_eq, comparator_4_eq);
  Comparator #(.width(3), .mode("unsigned")) comparator_4 (
    .a(instruction[2:0]), .b(3'b111), .eq(comparator_4_eq));  // open: gt, lt
  Comparator #(.mode("unsigned")) comparator_5 (
    .a(instruction[15:8]), .b(8'h27), .eq(comparator_5_eq));  // open: gt, lt
  Comparator #(.width(10), .mode("unsigned")) comparator_6 (
    .a(instruction[15:6]), .b(10'h100), .eq(and_r_r));  // open: gt, lt
  Comparator #(.width(5), .mode("unsigned")) comparator_7 (
    .a(instruction[15:11]), .b(5'b00010), .eq(asr_r_r_imm));  // open: gt, lt
  Comparator #(.width(5), .mode("unsigned")) comparator_8 (
    .a(instruction[15:11]), .b({5{1'b0}}), .eq(lsl_r_r_imm));  // open: gt, lt
  Comparator #(.width(5), .mode("unsigned")) comparator_9 (
    .a(instruction[15:11]), .b(5'b00001), .eq(lsr_r_r_imm));  // open: gt, lt
  Comparator #(.width(7), .mode("unsigned")) comparator_10 (
    .a(instruction[15:9]), .b(7'b0001101), .eq(sub_r_r_r));  // open: gt, lt
  Comparator #(.width(7), .mode("unsigned")) comparator_11 (
    .a(instruction[15:9]), .b(7'b0001111), .eq(sub_r_r_imm));  // open: gt, lt
  Comparator #(.width(5), .mode("unsigned")) comparator_12 (
    .a(instruction[15:11]), .b(5'b10001), .eq(ldrh_r_r_imm));  // open: gt, lt
  Comparator #(.width(7), .mode("unsigned")) comparator_13 (
    .a(instruction[15:9]), .b(7'b0101101), .eq(ldrh_r_r_r));  // open: gt, lt
  Comparator #(.width(5), .mode("unsigned")) comparator_14 (
    .a(instruction[15:11]), .b(5'b10000), .eq(strh_r_r_imm));  // open: gt, lt
  Comparator #(.width(7), .mode("unsigned")) comparator_15 (
    .a(instruction[15:9]), .b(7'b0101001), .eq(strh_r_r_r));  // open: gt, lt
  Comparator #(.width(4), .mode("unsigned")) comparator_16 (
    .a(instruction[15:12]), .b(4'b1101), .eq(b_cond));  // open: gt, lt
  Comparator #(.width(5), .mode("unsigned")) comparator_17 (
    .a(instruction[15:11]), .b(5'b11100), .eq(b_incond));  // open: gt, lt
  or or_1 (mov_pc, and_1_out, comparator_5_eq);
  Comparator #(.width(10), .mode("unsigned")) comparator_18 (
    .a(instruction[15:6]), .b(10'h10b), .eq(cmn_r_r));  // open: gt, lt
  Comparator #(.width(5), .mode("unsigned")) comparator_19 (
    .a(instruction[15:11]), .b(5'b00101), .eq(cmp_r_imm));  // open: gt, lt
  Comparator #(.width(10), .mode("unsigned")) comparator_20 (
    .a(instruction[15:6]), .b(10'h10a), .eq(cmp_r_r));  // open: gt, lt
  Comparator #(.width(10), .mode("unsigned")) comparator_21 (
    .a(instruction[15:6]), .b(10'h105), .eq(adc_r_r));  // open: gt, lt
  Comparator #(.width(5), .mode("unsigned")) comparator_22 (
    .a(instruction[15:11]), .b(5'b00110), .eq(add_r_imm));  // open: gt, lt
  Comparator #(.width(10), .mode("unsigned")) comparator_23 (
    .a(instruction[15:6]), .b(10'h104), .eq(asr_r_r));  // open: gt, lt
  Comparator #(.width(10), .mode("unsigned")) comparator_24 (
    .a(instruction[15:6]), .b(10'h101), .eq(eor_r_r));  // open: gt, lt
  Comparator #(.width(10), .mode("unsigned")) comparator_25 (
    .a(instruction[15:6]), .b(10'h102), .eq(lsl_r_r));  // open: gt, lt
  Comparator #(.width(10), .mode("unsigned")) comparator_26 (
    .a(instruction[15:6]), .b(10'h103), .eq(lsr_r_r));  // open: gt, lt
  Comparator #(.width(10), .mode("unsigned")) comparator_27 (
    .a(instruction[15:6]), .b(10'h10f), .eq(mvn_r_r));  // open: gt, lt
  Comparator #(.width(10), .mode("unsigned")) comparator_28 (
    .a(instruction[15:6]), .b(10'h109), .eq(neg_r_r));  // open: gt, lt
  Comparator #(.width(10), .mode("unsigned")) comparator_29 (
    .a(instruction[15:6]), .b(10'h10c), .eq(orr_r_r));  // open: gt, lt
  Comparator #(.width(10), .mode("unsigned")) comparator_30 (
    .a(instruction[15:6]), .b(10'h106), .eq(sbc_r_r));  // open: gt, lt
  Comparator #(.width(5), .mode("unsigned")) comparator_31 (
    .a(instruction[15:11]), .b(5'b00111), .eq(sub_r_imm));  // open: gt, lt
  Comparator #(.width(5), .mode("unsigned")) comparator_32 (
    .a(instruction[15:11]), .b(5'b01111), .eq(ldrb_r_r_imm));  // open: gt, lt
  Comparator #(.width(7), .mode("unsigned")) comparator_33 (
    .a(instruction[15:9]), .b(7'b0101110), .eq(ldrb_r_r_r));  // open: gt, lt
  Comparator #(.width(5), .mode("unsigned")) comparator_34 (
    .a(instruction[15:11]), .b(5'b01110), .eq(strb_r_r_imm));  // open: gt, lt
  Comparator #(.width(7), .mode("unsigned")) comparator_35 (
    .a(instruction[15:9]), .b(7'b0101010), .eq(strb_r_r_r));  // open: gt, lt
  Comparator #(.width(10), .mode("unsigned")) comparator_36 (
    .a(instruction[15:6]), .b(10'h10e), .eq(bic_r_r));  // open: gt, lt
  Comparator #(.width(10), .mode("unsigned")) comparator_37 (
    .a(instruction[15:6]), .b(10'h118), .eq(cpy_r_r));  // open: gt, lt
  Comparator #(.width(5), .mode("unsigned")) comparator_38 (
    .a(instruction[15:11]), .b(5'b00100), .eq(mov_r_imm));  // open: gt, lt
  Comparator #(.width(10), .mode("unsigned")) comparator_39 (
    .a(instruction[15:6]), .b(10'h10d), .eq(mul_r_r));  // open: gt, lt
  Comparator #(.width(10), .mode("unsigned")) comparator_40 (
    .a(instruction[15:6]), .b(10'h107), .eq(ror_r_r));  // open: gt, lt
  Comparator #(.width(10), .mode("unsigned")) comparator_41 (
    .a(instruction[15:6]), .b(10'h108), .eq(tst_r_r));  // open: gt, lt
  Comparator #(.width(5), .mode("unsigned")) comparator_42 (
    .a(instruction[15:11]), .b(5'b11110), .eq(bl_msb));  // open: gt, lt
  Comparator #(.width(5), .mode("unsigned")) comparator_43 (
    .a(instruction[15:11]), .b({5{1'b1}}), .eq(bl_lsb));  // open: gt, lt
  Comparator #(.width(9), .mode("unsigned")) comparator_44 (.a(instruction[15:7]), .b(9'h8e), .eq(bx));  // open: gt, lt

  // Notes on the sheet:
  //   OPCODE DECODER v.1.1
  //   Le signal de la bonne instruction est généré si on la détecte.
  //   Comparaison entre l'instruction et les différentes valeurs possible de celle-ci.
  //   ADD Rd, Rn, Rm
  //   ADD Rd, Rn, #0 to 7
  //   MOV PC, Rm
  //   MOV PC, #0 to 255
  //   AND Rd, Rm
  //   ASR Rd, Rm, #1 to 32
  //   LSL Rd, Rm, #0 to 31
  //   LSR Rd, Rm, #1 to 32
  //   SUB Rd, Rn, Rm
  //   SUB Rd, Rn, #0 to 7
  //   LDRH Rd, [Rn, #0 to 31 * 2]
  //   LDRH Rd, [Rn, Rm]
  //   STRH Rd, [Rn, #0 to 31 * 2]
  //   STRH Rd, [Rn, Rm]
  //   B<cond> <target_address>
  //   B <target_address>
  //   CMN Rd, Rm
  //   CMP Rn, #8
  //   CMP Rn, Rm
  //   ADC Rd, Rm
  //   ADD Rd, #0 to 255
  //   ASR Rd, Rs
  //   EOR Rd, Rm
  //   LSL Rd, Rs
  //   LSR Rd, Rs
  //   MVN Rd, Rm
  //   NEG Rd, Rm
  //   ORR Rd, Rm
  //   SBC Rd, Rm
  //   SUB Rd, #0 to 255
  //   LDRB Rd, [Rn, #0 to 31]
  //   LDRB Rd, [Rn, Rm]
  //   STRB Rd, [Rn, #0 to 31]
  //   STRB Rd, [Rn, Rm]
  //   BIC Rd, Rm
  //   CPY Rd, Rn
  //   MOV Rd, #0 to 255
  //   MUL Rd, Rm
  //   ROR Rd, Rs
  //   TST Rd, Rm
  //   BL 5bits MSB
  //   BL 11bits LSB
  //   BX R6
endmodule

module Decode_Control (
  input  [15:0] instruction_in,
  output [15:0] instruction_out,
  output link_en,
  output [1:0] sel_rn,
  output sel_rm,
  output reg_bank_en,
  output reg_mem_data_en
);

  wire decode_opcode_1_adc_r_r, decode_opcode_1_add_r_imm, decode_opcode_1_add_r_r_imm,
       decode_opcode_1_add_r_r_r, decode_opcode_1_and_r_r, decode_opcode_1_asr_r_r,
       decode_opcode_1_asr_r_r_imm, decode_opcode_1_b_cond, decode_opcode_1_b_incond,
       decode_opcode_1_bic_r_r, decode_opcode_1_bl_msb, decode_opcode_1_bx, decode_opcode_1_cmn_r_r,
       decode_opcode_1_cmp_r_imm, decode_opcode_1_cmp_r_r, decode_opcode_1_cpy_r_r, decode_opcode_1_eor_r_r,
       decode_opcode_1_ldrb_r_r_imm, decode_opcode_1_ldrb_r_r_r, decode_opcode_1_ldrh_r_r_imm,
       decode_opcode_1_ldrh_r_r_r, decode_opcode_1_lsl_r_r, decode_opcode_1_lsl_r_r_imm,
       decode_opcode_1_lsr_r_r, decode_opcode_1_lsr_r_r_imm, decode_opcode_1_mov_r_imm,
       decode_opcode_1_mul_r_r, decode_opcode_1_mvn_r_r, decode_opcode_1_neg_r_r, decode_opcode_1_orr_r_r,
       decode_opcode_1_ror_r_r, decode_opcode_1_sbc_r_r, decode_opcode_1_strb_r_r_imm,
       decode_opcode_1_strb_r_r_r, decode_opcode_1_strh_r_r_imm, decode_opcode_1_strh_r_r_r,
       decode_opcode_1_sub_r_imm, decode_opcode_1_sub_r_r_imm, decode_opcode_1_sub_r_r_r,
       decode_opcode_1_tst_r_r, reg_bank_en_2_out, reg_bank_en_out;

  // Text text_1: pin names not known
  // Text text_2: pin names not known
  // Text text_3: pin names not known
  // Text text_4: pin names not known
  // Text text_5: pin names not known
  Decode_Opcode decode_opcode_1 (
    .instruction(instruction_in), .add_r_r_r(decode_opcode_1_add_r_r_r),
    .add_r_r_imm(decode_opcode_1_add_r_r_imm), .and_r_r(decode_opcode_1_and_r_r),
    .asr_r_r_imm(decode_opcode_1_asr_r_r_imm), .lsl_r_r_imm(decode_opcode_1_lsl_r_r_imm),
    .lsr_r_r_imm(decode_opcode_1_lsr_r_r_imm), .sub_r_r_r(decode_opcode_1_sub_r_r_r),
    .sub_r_r_imm(decode_opcode_1_sub_r_r_imm), .ldrh_r_r_imm(decode_opcode_1_ldrh_r_r_imm),
    .ldrh_r_r_r(decode_opcode_1_ldrh_r_r_r), .strh_r_r_imm(decode_opcode_1_strh_r_r_imm),
    .strh_r_r_r(decode_opcode_1_strh_r_r_r), .b_cond(decode_opcode_1_b_cond),
    .b_incond(decode_opcode_1_b_incond), .adc_r_r(decode_opcode_1_adc_r_r),
    .cmn_r_r(decode_opcode_1_cmn_r_r), .cmp_r_imm(decode_opcode_1_cmp_r_imm),
    .cmp_r_r(decode_opcode_1_cmp_r_r), .add_r_imm(decode_opcode_1_add_r_imm),
    .asr_r_r(decode_opcode_1_asr_r_r), .eor_r_r(decode_opcode_1_eor_r_r), .lsl_r_r(decode_opcode_1_lsl_r_r),
    .lsr_r_r(decode_opcode_1_lsr_r_r), .mvn_r_r(decode_opcode_1_mvn_r_r), .neg_r_r(decode_opcode_1_neg_r_r),
    .orr_r_r(decode_opcode_1_orr_r_r), .sbc_r_r(decode_opcode_1_sbc_r_r),
    .sub_r_imm(decode_opcode_1_sub_r_imm), .ldrb_r_r_imm(decode_opcode_1_ldrb_r_r_imm),
    .strb_r_r_imm(decode_opcode_1_strb_r_r_imm), .ldrb_r_r_r(decode_opcode_1_ldrb_r_r_r),
    .strb_r_r_r(decode_opcode_1_strb_r_r_r), .bic_r_r(decode_opcode_1_bic_r_r),
    .cpy_r_r(decode_opcode_1_cpy_r_r), .mov_r_imm(decode_opcode_1_mov_r_imm),
    .mul_r_r(decode_opcode_1_mul_r_r), .ror_r_r(decode_opcode_1_ror_r_r), .tst_r_r(decode_opcode_1_tst_r_r),
    .bl_msb(decode_opcode_1_bl_msb), .bl_lsb(link_en), .bx(decode_opcode_1_bx));  // open: mov_pc
  or bit1 (sel_rn[1], decode_opcode_1_b_cond, decode_opcode_1_b_incond, decode_opcode_1_cmp_r_imm, decode_opcode_1_add_r_imm, decode_opcode_1_sub_r_imm, decode_opcode_1_mov_r_imm, decode_opcode_1_bl_msb);
  or bit0 (sel_rn[0], decode_opcode_1_and_r_r, decode_opcode_1_b_cond, decode_opcode_1_b_incond, decode_opcode_1_cmn_r_r, decode_opcode_1_cmp_r_r, decode_opcode_1_adc_r_r, decode_opcode_1_asr_r_r, decode_opcode_1_eor_r_r, decode_opcode_1_lsl_r_r, decode_opcode_1_lsr_r_r, decode_opcode_1_orr_r_r, decode_opcode_1_sbc_r_r, decode_opcode_1_bic_r_r, decode_opcode_1_mul_r_r, decode_opcode_1_ror_r_r, decode_opcode_1_tst_r_r, decode_opcode_1_bl_msb);
  or u_sel_rm (sel_rm, decode_opcode_1_and_r_r, decode_opcode_1_cmn_r_r, decode_opcode_1_cmp_r_r, decode_opcode_1_adc_r_r, decode_opcode_1_asr_r_r, decode_opcode_1_eor_r_r, decode_opcode_1_lsl_r_r, decode_opcode_1_lsr_r_r, decode_opcode_1_neg_r_r, decode_opcode_1_orr_r_r, decode_opcode_1_sbc_r_r, decode_opcode_1_bic_r_r, decode_opcode_1_cpy_r_r, decode_opcode_1_mul_r_r, decode_opcode_1_ror_r_r, decode_opcode_1_tst_r_r);
  or u_reg_bank_en (reg_bank_en_out, decode_opcode_1_add_r_r_r, decode_opcode_1_add_r_r_imm, decode_opcode_1_and_r_r, decode_opcode_1_asr_r_r_imm, decode_opcode_1_lsl_r_r_imm, decode_opcode_1_lsr_r_r_imm, decode_opcode_1_sub_r_r_r, decode_opcode_1_sub_r_r_imm, decode_opcode_1_ldrh_r_r_imm, decode_opcode_1_ldrh_r_r_r, decode_opcode_1_strh_r_r_imm, decode_opcode_1_strh_r_r_r, decode_opcode_1_b_cond, decode_opcode_1_b_incond, decode_opcode_1_cmn_r_r, decode_opcode_1_cmp_r_imm, decode_opcode_1_cmp_r_r, decode_opcode_1_adc_r_r, decode_opcode_1_add_r_imm, decode_opcode_1_asr_r_r);
  or or_1 (reg_bank_en, reg_bank_en_out, reg_bank_en_2_out);
  or reg_bank_en_2 (reg_bank_en_2_out, decode_opcode_1_eor_r_r, decode_opcode_1_lsl_r_r, decode_opcode_1_lsr_r_r, decode_opcode_1_mvn_r_r, decode_opcode_1_neg_r_r, decode_opcode_1_orr_r_r, decode_opcode_1_sbc_r_r, decode_opcode_1_sub_r_imm, decode_opcode_1_ldrb_r_r_imm, decode_opcode_1_ldrb_r_r_r, decode_opcode_1_strb_r_r_imm, decode_opcode_1_strb_r_r_r, decode_opcode_1_bic_r_r, decode_opcode_1_cpy_r_r, decode_opcode_1_mov_r_imm, decode_opcode_1_mul_r_r, decode_opcode_1_ror_r_r, decode_opcode_1_tst_r_r, decode_opcode_1_bl_msb, link_en, decode_opcode_1_bx);
  or u_reg_mem_data_en (reg_mem_data_en, decode_opcode_1_strh_r_r_imm, decode_opcode_1_strh_r_r_r, decode_opcode_1_strb_r_r_imm, decode_opcode_1_strb_r_r_r);

  assign instruction_out = instruction_in;
endmodule

module Execute_Control (
  input  [15:0] instruction_in,
  output [15:0] instruction_out,
  output [2:0] sel_op_shift,
  output sel_shift,
  output [3:0] sel_op_alu,
  output [1:0] sel_operand_1,
  output [1:0] sel_operand_2,
  output [2:0] sel_mult_2,
  output [1:0] sel_carry,
  output cond_en,
  output cond_en_2,
  output flag_z_en,
  output flag_n_en,
  output flag_c_en,
  output flag_v_en,
  output sel_cpsr
);

  wire decode_opcode_1_add_r_imm, decode_opcode_1_add_r_r_imm, decode_opcode_1_add_r_r_r,
       decode_opcode_1_and_r_r, decode_opcode_1_asr_r_r, decode_opcode_1_asr_r_r_imm,
       decode_opcode_1_b_incond, decode_opcode_1_bic_r_r, decode_opcode_1_bl_msb, decode_opcode_1_bx,
       decode_opcode_1_cmn_r_r, decode_opcode_1_cmp_r_imm, decode_opcode_1_cmp_r_r, decode_opcode_1_cpy_r_r,
       decode_opcode_1_eor_r_r, decode_opcode_1_ldrb_r_r_imm, decode_opcode_1_ldrb_r_r_r,
       decode_opcode_1_ldrh_r_r_imm, decode_opcode_1_ldrh_r_r_r, decode_opcode_1_lsl_r_r,
       decode_opcode_1_lsl_r_r_imm, decode_opcode_1_lsr_r_r, decode_opcode_1_lsr_r_r_imm,
       decode_opcode_1_mov_r_imm, decode_opcode_1_mvn_r_r, decode_opcode_1_neg_r_r, decode_opcode_1_orr_r_r,
       decode_opcode_1_strb_r_r_imm, decode_opcode_1_strb_r_r_r, decode_opcode_1_strh_r_r_imm,
       decode_opcode_1_strh_r_r_r, decode_opcode_1_sub_r_imm, decode_opcode_1_sub_r_r_imm,
       decode_opcode_1_sub_r_r_r, decode_opcode_1_tst_r_r;

  // Text text_1: pin names not known
  // Text text_2: pin names not known
  // Text text_3: pin names not known
  // Text text_4: pin names not known
  // Text text_5: pin names not known
  Decode_Opcode decode_opcode_1 (
    .instruction(instruction_in), .add_r_r_r(decode_opcode_1_add_r_r_r),
    .add_r_r_imm(decode_opcode_1_add_r_r_imm), .and_r_r(decode_opcode_1_and_r_r),
    .asr_r_r_imm(decode_opcode_1_asr_r_r_imm), .lsl_r_r_imm(decode_opcode_1_lsl_r_r_imm),
    .lsr_r_r_imm(decode_opcode_1_lsr_r_r_imm), .sub_r_r_r(decode_opcode_1_sub_r_r_r),
    .sub_r_r_imm(decode_opcode_1_sub_r_r_imm), .ldrh_r_r_imm(decode_opcode_1_ldrh_r_r_imm),
    .ldrh_r_r_r(decode_opcode_1_ldrh_r_r_r), .strh_r_r_imm(decode_opcode_1_strh_r_r_imm),
    .strh_r_r_r(decode_opcode_1_strh_r_r_r), .b_cond(cond_en), .b_incond(decode_opcode_1_b_incond),
    .adc_r_r(sel_carry[0]), .cmn_r_r(decode_opcode_1_cmn_r_r), .cmp_r_imm(decode_opcode_1_cmp_r_imm),
    .cmp_r_r(decode_opcode_1_cmp_r_r), .add_r_imm(decode_opcode_1_add_r_imm),
    .asr_r_r(decode_opcode_1_asr_r_r), .eor_r_r(decode_opcode_1_eor_r_r), .lsl_r_r(decode_opcode_1_lsl_r_r),
    .lsr_r_r(decode_opcode_1_lsr_r_r), .mvn_r_r(decode_opcode_1_mvn_r_r), .neg_r_r(decode_opcode_1_neg_r_r),
    .orr_r_r(decode_opcode_1_orr_r_r), .sbc_r_r(sel_carry[1]), .sub_r_imm(decode_opcode_1_sub_r_imm),
    .ldrb_r_r_imm(decode_opcode_1_ldrb_r_r_imm), .strb_r_r_imm(decode_opcode_1_strb_r_r_imm),
    .ldrb_r_r_r(decode_opcode_1_ldrb_r_r_r), .strb_r_r_r(decode_opcode_1_strb_r_r_r),
    .bic_r_r(decode_opcode_1_bic_r_r), .cpy_r_r(decode_opcode_1_cpy_r_r),
    .mov_r_imm(decode_opcode_1_mov_r_imm), .mul_r_r(sel_op_alu[3]), .ror_r_r(sel_op_shift[2]),
    .tst_r_r(decode_opcode_1_tst_r_r), .bl_msb(decode_opcode_1_bl_msb), .bl_lsb(sel_operand_1[1]),
    .bx(decode_opcode_1_bx), .mov_pc(sel_cpsr));
  or bit1 (sel_op_shift[1], decode_opcode_1_lsl_r_r_imm, decode_opcode_1_lsr_r_r_imm, decode_opcode_1_lsl_r_r, decode_opcode_1_lsr_r_r);
  or bit0 (sel_op_shift[0], decode_opcode_1_asr_r_r_imm, decode_opcode_1_lsr_r_r_imm, decode_opcode_1_asr_r_r, decode_opcode_1_lsr_r_r);
  or u_sel_shift (sel_shift, decode_opcode_1_asr_r_r, decode_opcode_1_lsl_r_r, decode_opcode_1_lsr_r_r, sel_op_shift[2]);
  or bit2 (sel_op_alu[2], decode_opcode_1_eor_r_r, decode_opcode_1_mvn_r_r, decode_opcode_1_orr_r_r, decode_opcode_1_bic_r_r);
  or bit1_2 (sel_op_alu[1], decode_opcode_1_and_r_r, decode_opcode_1_sub_r_r_r, decode_opcode_1_sub_r_r_imm, decode_opcode_1_cmp_r_imm, decode_opcode_1_cmp_r_r, decode_opcode_1_mvn_r_r, decode_opcode_1_neg_r_r, sel_carry[1], decode_opcode_1_sub_r_imm, decode_opcode_1_bic_r_r, decode_opcode_1_tst_r_r);
  or bit0_2 (sel_op_alu[0], decode_opcode_1_add_r_r_r, decode_opcode_1_add_r_r_imm, decode_opcode_1_and_r_r, decode_opcode_1_ldrh_r_r_imm, decode_opcode_1_ldrh_r_r_r, decode_opcode_1_strh_r_r_imm, decode_opcode_1_strh_r_r_r, cond_en, decode_opcode_1_b_incond, decode_opcode_1_cmn_r_r, sel_carry[0], decode_opcode_1_add_r_imm, decode_opcode_1_eor_r_r, decode_opcode_1_ldrb_r_r_imm, decode_opcode_1_ldrb_r_r_r, decode_opcode_1_strb_r_r_imm, decode_opcode_1_strb_r_r_r, decode_opcode_1_bic_r_r, decode_opcode_1_cpy_r_r, decode_opcode_1_mov_r_imm, decode_opcode_1_tst_r_r, decode_opcode_1_bl_msb, sel_operand_1[1]);
  or bit0_3 (sel_operand_1[0], decode_opcode_1_neg_r_r, decode_opcode_1_mov_r_imm, decode_opcode_1_cpy_r_r);
  or bit1_3 (sel_operand_2[1], decode_opcode_1_ldrh_r_r_imm, decode_opcode_1_strh_r_r_imm, cond_en, decode_opcode_1_b_incond, decode_opcode_1_cmp_r_imm, decode_opcode_1_add_r_imm, decode_opcode_1_sub_r_imm, decode_opcode_1_ldrb_r_r_imm, decode_opcode_1_strb_r_r_imm, decode_opcode_1_mov_r_imm, decode_opcode_1_bl_msb, sel_operand_1[1]);
  or bit0_4 (sel_operand_2[0], decode_opcode_1_add_r_r_imm, decode_opcode_1_sub_r_r_imm, decode_opcode_1_cmp_r_imm, decode_opcode_1_add_r_imm, decode_opcode_1_sub_r_imm, decode_opcode_1_mov_r_imm);
  or bit2_2 (sel_mult_2[2], decode_opcode_1_ldrb_r_r_imm, decode_opcode_1_strb_r_r_imm, decode_opcode_1_bl_msb);
  or bit1_4 (sel_mult_2[1], cond_en, sel_operand_1[1]);
  or bit0_5 (sel_mult_2[0], decode_opcode_1_b_incond, decode_opcode_1_bl_msb, sel_operand_1[1]);
  or c_unaffected (cond_en_2, decode_opcode_1_lsl_r_r_imm, decode_opcode_1_asr_r_r, decode_opcode_1_lsl_r_r, decode_opcode_1_lsr_r_r);
  or u_flag_z_en (flag_z_en, decode_opcode_1_add_r_r_r, decode_opcode_1_add_r_r_imm, decode_opcode_1_and_r_r, decode_opcode_1_asr_r_r_imm, decode_opcode_1_lsl_r_r_imm, decode_opcode_1_lsr_r_r_imm, decode_opcode_1_sub_r_r_r, decode_opcode_1_sub_r_r_imm, decode_opcode_1_cmn_r_r, decode_opcode_1_cmp_r_imm, decode_opcode_1_cmp_r_r, sel_carry[0], decode_opcode_1_add_r_imm, decode_opcode_1_asr_r_r, decode_opcode_1_eor_r_r, decode_opcode_1_lsl_r_r, decode_opcode_1_lsr_r_r, decode_opcode_1_mvn_r_r, decode_opcode_1_neg_r_r, decode_opcode_1_orr_r_r, sel_carry[1], decode_opcode_1_sub_r_imm, decode_opcode_1_bic_r_r, decode_opcode_1_mov_r_imm, sel_op_alu[3], sel_op_shift[2], decode_opcode_1_tst_r_r, decode_opcode_1_bx, sel_cpsr);
  or u_flag_n_en (flag_n_en, decode_opcode_1_add_r_r_r, decode_opcode_1_add_r_r_imm, decode_opcode_1_and_r_r, decode_opcode_1_asr_r_r_imm, decode_opcode_1_lsl_r_r_imm, decode_opcode_1_lsr_r_r_imm, decode_opcode_1_sub_r_r_r, decode_opcode_1_sub_r_r_imm, decode_opcode_1_cmn_r_r, decode_opcode_1_cmp_r_imm, decode_opcode_1_cmp_r_r, sel_carry[0], decode_opcode_1_add_r_imm, decode_opcode_1_asr_r_r, decode_opcode_1_eor_r_r, decode_opcode_1_lsl_r_r, decode_opcode_1_lsr_r_r, decode_opcode_1_mvn_r_r, decode_opcode_1_neg_r_r, decode_opcode_1_orr_r_r, sel_carry[1], decode_opcode_1_sub_r_imm, decode_opcode_1_bic_r_r, decode_opcode_1_mov_r_imm, sel_op_alu[3], sel_op_shift[2], decode_opcode_1_tst_r_r, decode_opcode_1_bx, sel_cpsr);
  or u_flag_c_en (flag_c_en, decode_opcode_1_add_r_r_r, decode_opcode_1_add_r_r_imm, decode_opcode_1_asr_r_r_imm, decode_opcode_1_lsl_r_r_imm, decode_opcode_1_lsr_r_r_imm, decode_opcode_1_sub_r_r_r, decode_opcode_1_sub_r_r_imm, decode_opcode_1_cmn_r_r, decode_opcode_1_cmp_r_imm, decode_opcode_1_cmp_r_r, sel_carry[0], decode_opcode_1_add_r_imm, decode_opcode_1_asr_r_r, decode_opcode_1_lsl_r_r, decode_opcode_1_lsr_r_r, decode_opcode_1_neg_r_r, sel_carry[1], decode_opcode_1_sub_r_imm, sel_op_shift[2], decode_opcode_1_bx, sel_cpsr);
  or u_flag_v_en (flag_v_en, decode_opcode_1_add_r_r_r, decode_opcode_1_add_r_r_imm, decode_opcode_1_sub_r_r_r, decode_opcode_1_sub_r_r_imm, decode_opcode_1_cmn_r_r, decode_opcode_1_cmp_r_imm, decode_opcode_1_cmp_r_r, sel_carry[0], decode_opcode_1_add_r_imm, decode_opcode_1_neg_r_r, sel_carry[1], decode_opcode_1_sub_r_imm, decode_opcode_1_bx, sel_cpsr);

  assign instruction_out = instruction_in;
endmodule

module Memory_Control (
  input  [15:0] instruction_in,
  output [15:0] instruction_out,
  output \byte ,
  output sel_mem,
  output str_data,
  output ldr_data
);

  wire decode_opcode_1_ldrb_r_r_imm, decode_opcode_1_ldrb_r_r_r, decode_opcode_1_ldrh_r_r_imm,
       decode_opcode_1_ldrh_r_r_r, decode_opcode_1_strb_r_r_imm, decode_opcode_1_strb_r_r_r,
       decode_opcode_1_strh_r_r_imm, decode_opcode_1_strh_r_r_r;

  // Text text_1: pin names not known
  // Text text_2: pin names not known
  // Text text_3: pin names not known
  // Text text_4: pin names not known
  // Text text_5: pin names not known
  Decode_Opcode decode_opcode_1 (
    .instruction(instruction_in), .ldrh_r_r_imm(decode_opcode_1_ldrh_r_r_imm),
    .ldrh_r_r_r(decode_opcode_1_ldrh_r_r_r), .strh_r_r_imm(decode_opcode_1_strh_r_r_imm),
    .strh_r_r_r(decode_opcode_1_strh_r_r_r), .ldrb_r_r_imm(decode_opcode_1_ldrb_r_r_imm),
    .strb_r_r_imm(decode_opcode_1_strb_r_r_imm), .ldrb_r_r_r(decode_opcode_1_ldrb_r_r_r),
    .strb_r_r_r(decode_opcode_1_strb_r_r_r));  // open: add_r_r_r, add_r_r_imm, and_r_r, asr_r_r_imm, lsl_r_r_imm, lsr_r_r_imm, sub_r_r_r, sub_r_r_imm, b_cond, b_incond, adc_r_r, cmn_r_r, cmp_r_imm, cmp_r_r, add_r_imm, asr_r_r, eor_r_r, lsl_r_r, lsr_r_r, mvn_r_r, neg_r_r, orr_r_r, sbc_r_r, sub_r_imm, bic_r_r, cpy_r_r, mov_r_imm, mul_r_r, ror_r_r, tst_r_r, bl_msb, bl_lsb, bx, mov_pc
  or u_sel_mem (\byte , decode_opcode_1_ldrb_r_r_imm, decode_opcode_1_ldrb_r_r_r, decode_opcode_1_strb_r_r_imm, decode_opcode_1_strb_r_r_r);
  or sel_mem_2 (sel_mem, decode_opcode_1_ldrh_r_r_imm, decode_opcode_1_ldrh_r_r_r, decode_opcode_1_ldrb_r_r_imm, decode_opcode_1_ldrb_r_r_r);
  or u_str_data (str_data, decode_opcode_1_strh_r_r_imm, decode_opcode_1_strh_r_r_r, decode_opcode_1_strb_r_r_imm, decode_opcode_1_strb_r_r_r);
  or u_ldr_data (ldr_data, decode_opcode_1_ldrh_r_r_imm, decode_opcode_1_ldrh_r_r_r, decode_opcode_1_ldrb_r_r_imm, decode_opcode_1_ldrb_r_r_r);

  assign instruction_out = instruction_in;
endmodule

module Writeback_Control (
  input  [15:0] instruction_in,
  output reg_bank_wr,
  output sel_PC
);

  wire decode_opcode_1_adc_r_r, decode_opcode_1_add_r_imm, decode_opcode_1_add_r_r_imm,
       decode_opcode_1_add_r_r_r, decode_opcode_1_and_r_r, decode_opcode_1_asr_r_r,
       decode_opcode_1_asr_r_r_imm, decode_opcode_1_b_cond, decode_opcode_1_b_incond,
       decode_opcode_1_bic_r_r, decode_opcode_1_bl_lsb, decode_opcode_1_cpy_r_r, decode_opcode_1_eor_r_r,
       decode_opcode_1_ldrb_r_r_imm, decode_opcode_1_ldrb_r_r_r, decode_opcode_1_ldrh_r_r_imm,
       decode_opcode_1_ldrh_r_r_r, decode_opcode_1_lsl_r_r, decode_opcode_1_lsl_r_r_imm,
       decode_opcode_1_lsr_r_r, decode_opcode_1_lsr_r_r_imm, decode_opcode_1_mov_pc,
       decode_opcode_1_mov_r_imm, decode_opcode_1_mul_r_r, decode_opcode_1_mvn_r_r, decode_opcode_1_neg_r_r,
       decode_opcode_1_orr_r_r, decode_opcode_1_ror_r_r, decode_opcode_1_sbc_r_r, decode_opcode_1_sub_r_imm,
       decode_opcode_1_sub_r_r_imm, decode_opcode_1_sub_r_r_r;

  // Text text_1: pin names not known
  // Text text_2: pin names not known
  // Text text_3: pin names not known
  // Text text_4: pin names not known
  // Text text_5: pin names not known
  Decode_Opcode decode_opcode_1 (
    .instruction(instruction_in), .add_r_r_r(decode_opcode_1_add_r_r_r),
    .add_r_r_imm(decode_opcode_1_add_r_r_imm), .and_r_r(decode_opcode_1_and_r_r),
    .asr_r_r_imm(decode_opcode_1_asr_r_r_imm), .lsl_r_r_imm(decode_opcode_1_lsl_r_r_imm),
    .lsr_r_r_imm(decode_opcode_1_lsr_r_r_imm), .sub_r_r_r(decode_opcode_1_sub_r_r_r),
    .sub_r_r_imm(decode_opcode_1_sub_r_r_imm), .ldrh_r_r_imm(decode_opcode_1_ldrh_r_r_imm),
    .ldrh_r_r_r(decode_opcode_1_ldrh_r_r_r), .b_cond(decode_opcode_1_b_cond),
    .b_incond(decode_opcode_1_b_incond), .adc_r_r(decode_opcode_1_adc_r_r),
    .add_r_imm(decode_opcode_1_add_r_imm), .asr_r_r(decode_opcode_1_asr_r_r),
    .eor_r_r(decode_opcode_1_eor_r_r), .lsl_r_r(decode_opcode_1_lsl_r_r), .lsr_r_r(decode_opcode_1_lsr_r_r),
    .mvn_r_r(decode_opcode_1_mvn_r_r), .neg_r_r(decode_opcode_1_neg_r_r), .orr_r_r(decode_opcode_1_orr_r_r),
    .sbc_r_r(decode_opcode_1_sbc_r_r), .sub_r_imm(decode_opcode_1_sub_r_imm),
    .ldrb_r_r_imm(decode_opcode_1_ldrb_r_r_imm), .ldrb_r_r_r(decode_opcode_1_ldrb_r_r_r),
    .bic_r_r(decode_opcode_1_bic_r_r), .cpy_r_r(decode_opcode_1_cpy_r_r),
    .mov_r_imm(decode_opcode_1_mov_r_imm), .mul_r_r(decode_opcode_1_mul_r_r),
    .ror_r_r(decode_opcode_1_ror_r_r), .bl_lsb(decode_opcode_1_bl_lsb), .mov_pc(decode_opcode_1_mov_pc));  // open: strh_r_r_imm, strh_r_r_r, cmn_r_r, cmp_r_imm, cmp_r_r, strb_r_r_imm, strb_r_r_r, tst_r_r, bl_msb, bx
  or u_reg_bank_wr (reg_bank_wr, decode_opcode_1_add_r_r_r, decode_opcode_1_add_r_r_imm, decode_opcode_1_and_r_r, decode_opcode_1_asr_r_r_imm, decode_opcode_1_lsl_r_r_imm, decode_opcode_1_lsr_r_r_imm, decode_opcode_1_sub_r_r_r, decode_opcode_1_sub_r_r_imm, decode_opcode_1_ldrh_r_r_imm, decode_opcode_1_ldrh_r_r_r, decode_opcode_1_adc_r_r, decode_opcode_1_add_r_imm, decode_opcode_1_asr_r_r, decode_opcode_1_eor_r_r, decode_opcode_1_lsl_r_r, decode_opcode_1_lsr_r_r, decode_opcode_1_mvn_r_r, decode_opcode_1_neg_r_r, decode_opcode_1_orr_r_r, decode_opcode_1_sbc_r_r, decode_opcode_1_sub_r_imm, decode_opcode_1_ldrb_r_r_imm, decode_opcode_1_ldrb_r_r_r, decode_opcode_1_bic_r_r, decode_opcode_1_cpy_r_r, decode_opcode_1_mov_r_imm, decode_opcode_1_mul_r_r, decode_opcode_1_ror_r_r, decode_opcode_1_mov_pc);
  or u_sel_PC (sel_PC, decode_opcode_1_b_cond, decode_opcode_1_b_incond, 1'b0, decode_opcode_1_bl_lsb);
endmodule

module Multi_2 (
  input  [4:0] immediate5,
  input  [2:0] sel_mul_2,
  input  [10:0] offset_incond,
  input  [7:0] offset_cond,
  output [15:0] Mult_2_out
);

  wire [15:0] adder_1_out, adder_2_out, adder_3_out, adder_4_out, bit_extender_1_out, bit_extender_2_out,
       bit_extender_3_out, bit_extender_4_out, multiplexer_1_out, shifter_1_out, shifter_2_out;

  // Text text_1: pin names not known
  // Text text_2: pin names not known
  // Text text_3: pin names not known
  // Text text_4: pin names not known
  // Text text_5: pin names not known
  assign bit_extender_1_out = {{11{immediate5[4]}}, immediate5};  // Bit_Extender bit_extender_1
  assign bit_extender_2_out = {{5{offset_incond[10]}}, offset_incond};  // Bit_Extender bit_extender_2
  assign bit_extender_3_out = {{5{offset_incond[10]}}, offset_incond};  // Bit_Extender bit_extender_3
  assign bit_extender_4_out = {{8{offset_cond[7]}}, offset_cond};  // Bit_Extender bit_extender_4
  Adder #(.width(16)) adder_1 (.a(bit_extender_2_out), .b(16'h2), .out(adder_1_out));  // open: cin, cout
  Adder #(.width(16)) adder_2 (.a(bit_extender_3_out), .b(16'h1), .out(adder_2_out));  // open: cin, cout
  Adder #(.width(16)) adder_3 (.a(bit_extender_4_out), .b(16'h2), .out(adder_3_out));  // open: cin, cout
  Multiplexer #(.select(2), .width(16), .enable("false")) multiplexer_1 (
    .in0(bit_extender_1_out), .in1(adder_1_out), .in2(adder_3_out), .in3(adder_2_out),
    .out(multiplexer_1_out), .sel(sel_mul_2[1:0]));
  Shifter #(.width(16)) shifter_1 (.in(bit_extender_2_out), .\dist (4'b1100), .out(shifter_1_out));
  Shifter #(.width(16)) shifter_2 (.in(multiplexer_1_out), .\dist (4'b0001), .out(shifter_2_out));
  Adder #(.width(16)) adder_4 (.a(shifter_1_out), .b(16'h2), .out(adder_4_out));  // open: cin, cout
  Multiplexer #(.select(3), .width(16), .enable("false")) multiplexer_2 (
    .in0(shifter_2_out), .in1(shifter_2_out), .in2(shifter_2_out), .in3(shifter_2_out),
    .in4(bit_extender_1_out), .in5(adder_4_out), .in6({16{1'b0}}), .in7({16{1'b0}}), .out(Mult_2_out),
    .sel(sel_mul_2));

  // Notes on the sheet:
  //   rajouté le bit de signe.
  //   Multi_2 v1.1
  //   alors que les offset servent aux instructions de branch.
  //   Ajout 1.1 : Ajout d'un shift de 11 gauche pour l'offset du BL MSB
  //   L'offset inconditionnelle a besoin des 2 extensions posibbles :
  //   Le branch classique peut faire des saut en arrière, et on a donc besoin d'une extension signée.
  //   Ce bloc sert à multiplier une des valeurs en entrée par 2. L'immediate5 sert pour les STR et LDR, 
  //   Le Branch avec Link peut utilisé cet offset en tant que LSB, et on l'additionnera ensuite au PC. Il ne faut donc pas 
  //   Correction du PC qui n'est pas pré-incrémenter
  //   pour LDRB et STRB.
  //   Permet de ne pas multiplier par 2 la valeur immediate sur 5 bits
  //   L'opération 100 est utilsée par BL MSB : On récupère les 5 bits MSB de l'offset décalé de 12 à gauche.
endmodule

module EXECUTE (
  input  [15:0] reg_data_out_n,
  input  [15:0] reg_data_out_m,
  input  [2:0] imm3,
  input  [7:0] offset_cond_or_imm8,
  input  [22:0] execute_control_bus,
  input  [4:0] imm5,
  output [15:0] OUT_EXECUTE
);

  wire comparator_1_eq, comparator_2_eq;
  wire [3:0] bitselector_3_out, bitselector_4_out, multiplexer_3_out, multiplexer_4_out;
  wire [15:0] bitselector_1_out, bitselector_2_out, lsl_inst_1_lsl_out, multiplexer_1_out, multiplexer_2_out,
       multiplexer_5_out;

  // Text text_1: pin names not known
  // Text text_2: pin names not known
  // Text text_3: pin names not known
  // Text text_4: pin names not known
  // Text text_5: pin names not known
  BitSelector #(.width(3), .group(16)) bitselector_1 (.in(imm3), .out(bitselector_1_out), .sel(1'b0));
  BitSelector #(.group(16)) bitselector_2 (.in(offset_cond_or_imm8), .out(bitselector_2_out), .sel(1'b0));
  BitSelector #(.width(5), .group(4)) bitselector_3 (.in(imm5), .out(bitselector_3_out), .sel(1'b0));
  BitSelector #(.width(16), .group(4)) bitselector_4 (.in(reg_data_out_m), .out(bitselector_4_out), .sel(2'b00));
  Multiplexer #(.select(2), .width(16), .enable("false")) multiplexer_1 (
    .in0(reg_data_out_n), .in1({16{1'b0}}), .in2({16{1'b0}}), .in3({16{1'b0}}), .out(multiplexer_1_out),
    .sel(execute_control_bus[10:9]));
  Multiplexer #(.select(2), .width(16), .enable("false")) multiplexer_2 (
    .in0(reg_data_out_m), .in1(bitselector_1_out), .in2({16{1'b0}}), .in3(bitselector_2_out),
    .out(multiplexer_2_out), .sel(execute_control_bus[8:7]));
  // Probe on execute_control_bus[10:9]
  Multiplexer #(.width(4), .enable("false")) multiplexer_3 (
    .in0(bitselector_3_out), .in1(bitselector_4_out), .out(multiplexer_3_out), .sel(execute_control_bus[20]));
  // Probe on execute_control_bus[2:0]
  Comparator #(.width(3)) comparator_1 (
    .a(execute_control_bus[2:0]), .b(3'b000), .eq(comparator_1_eq));  // open: gt, lt
  // Probe on multiplexer_1_out
  Multiplexer #(.width(4), .enable("false")) multiplexer_4 (
    .in0(multiplexer_3_out), .in1(4'b0000), .out(multiplexer_4_out), .sel(comparator_1_eq));
  // Probe on execute_control_bus[2:0]
  Multiplexer #(.width(16), .enable("false")) multiplexer_5 (
    .in0(multiplexer_2_out), .in1({16{1'b0}}), .out(multiplexer_5_out), .sel(comparator_2_eq));
  Comparator #(.width(4)) comparator_2 (
    .a(4'b0000), .b(execute_control_bus[6:3]), .eq(comparator_2_eq));  // open: gt, lt
  // Probe on multiplexer_5_out
  // Probe on execute_control_bus[6:3]
  LSL_INST lsl_inst_1 (
    .Op1(multiplexer_1_out), .sel_shift(multiplexer_4_out), .sel_op_shift(execute_control_bus[2:0]),
    .LSL_OUT(lsl_inst_1_lsl_out));
  // Probe on lsl_inst_1_lsl_out
  ALU alu_1 (
    .Op1(lsl_inst_1_lsl_out), .Op2(multiplexer_5_out), .sel_op_alu(execute_control_bus[6:3]),
    .OUT_ALU(OUT_EXECUTE));
endmodule

module COMP_INST (
  input  [15:0] Op1,
  input  [15:0] Op2,
  input  ACTIV,
  input  [2:0] op,
  output [15:0] COMP_OUT
);

  wire and_1_out, and_2_out, not_2_out;
  wire [15:0] and_3_out, demultiplexer_1_out0, multiplexer_1_out, multiplexer_2_out, multiplexer_3_out,
       not_1_out, not_3_out, or_1_out, xor_1_out;

  // Text text_1: pin names not known
  // Text text_2: pin names not known
  // Text text_3: pin names not known
  // Text text_4: pin names not known
  // Text text_5: pin names not known
  assign not_1_out = ~Op1;  // NOT_Gate not_1, 16 bits wide
  not not_2 (not_2_out, op[0]);
  Multiplexer #(.width(16), .enable("false")) multiplexer_1 (
    .in0(Op1), .in1(not_1_out), .out(multiplexer_1_out), .sel(and_1_out));
  assign not_3_out = ~Op2;  // NOT_Gate not_3, 16 bits wide
  and and_1 (and_1_out, not_2_out, op[1], op[2]);
  and and_2 (and_2_out, op[0], op[1], op[2]);
  Multiplexer #(.width(16), .enable("false")) multiplexer_2 (
    .in0(Op2), .in1(not_3_out), .out(multiplexer_2_out), .sel(and_2_out));
  assign and_3_out = multiplexer_1_out & multiplexer_2_out;  // AND_Gate and_3, 16 bits wide
  assign or_1_out = multiplexer_1_out | multiplexer_2_out;  // OR_Gate or_1, 16 bits wide
  assign xor_1_out = multiplexer_1_out ^ multiplexer_2_out;  // XOR_Gate xor_1, 16 bits wide
  Multiplexer #(.select(3), .width(16), .enable("false")) multiplexer_3 (
    .in0({16{1'b0}}), .in1({16{1'b0}}), .in2({16{1'b0}}), .in3(and_3_out), .in4(or_1_out), .in5(xor_1_out),
    .in6(multiplexer_1_out), .in7(and_3_out), .out(multiplexer_3_out), .sel(op));
  // Probe on multiplexer_3_out
  Demultiplexer #(.width(16), .enable("false")) demultiplexer_1 (
    .out0(demultiplexer_1_out0), .out1(COMP_OUT), .in(multiplexer_3_out), .sel(ACTIV));
  // also tied to GND on the sheet: {demultiplexer_1_out0[0], demultiplexer_1_out0[1], demultiplexer_1_out0[2], demultiplexer_1_out0[3], demultiplexer_1_out0[4], demultiplexer_1_out0[5], demultiplexer_1_out0[6], demultiplexer_1_out0[7], demultiplexer_1_out0[8], demultiplexer_1_out0[9], demultiplexer_1_out0[10], demultiplexer_1_out0[11], demultiplexer_1_out0[12], demultiplexer_1_out0[13], demultiplexer_1_out0[14], demultiplexer_1_out0[15]}
endmodule

module ALU (
  input  [15:0] Op1,
  input  [15:0] Op2,
  input  [3:0] sel_op_alu,
  output [15:0] OUT_ALU
);

  wire and_1_out, and_2_out, and_3_out, comparator_1_eq, not_1_out, not_2_out, not_3_out, not_4_out,
       not_5_out;
  wire [2:0] bitselector_1_out;
  wire [15:0] add_inst_1_add_out, comp_inst_1_comp_out, multiplexer_1_out, multiplexer_2_out,
       sub_inst_1_sub_out;

  // Text text_1: pin names not known
  // Text text_2: pin names not known
  // Text text_3: pin names not known
  // Text text_4: pin names not known
  // Text text_5: pin names not known
  BitSelector #(.width(4), .group(3)) bitselector_1 (
    .in({{2{sel_op_alu[3]}}, sel_op_alu[1:0]}), .out(bitselector_1_out), .sel(1'b0));
  Comparator #(.width(4)) comparator_1 (
    .a({{2{sel_op_alu[3]}}, sel_op_alu[1:0]}), .b(4'b0000), .eq(comparator_1_eq));  // open: gt, lt
  and and_1 (and_1_out, sel_op_alu[0], sel_op_alu[1], not_1_out);
  not not_1 (not_1_out, sel_op_alu[3]);
  not not_2 (not_2_out, sel_op_alu[1]);
  not not_3 (not_3_out, sel_op_alu[3]);
  not not_4 (not_4_out, sel_op_alu[3]);
  and and_2 (and_2_out, sel_op_alu[0], not_2_out, not_3_out, not_4_out);
  not not_5 (not_5_out, sel_op_alu[0]);
  and and_3 (and_3_out, not_5_out, sel_op_alu[1], not_3_out, not_4_out);
  COMP_INST comp_inst_1 (
    .Op1(Op1), .Op2(Op2), .ACTIV(and_1_out), .op(bitselector_1_out), .COMP_OUT(comp_inst_1_comp_out));
  ADD_INST add_inst_1 (.Op1(Op1), .Op2(Op2), .ACTIV(and_2_out), .ADD_OUT(add_inst_1_add_out));
  SUB_INST sub_inst_1 (.Op1(Op1), .Op2(Op2), .ACTIV(and_3_out), .SUB_OUT(sub_inst_1_sub_out));
  Multiplexer #(.width(16), .enable("false")) multiplexer_1 (
    .in0(add_inst_1_add_out), .in1(sub_inst_1_sub_out), .out(multiplexer_1_out), .sel(and_3_out));
  Multiplexer #(.width(16), .enable("false")) multiplexer_2 (
    .in0(multiplexer_1_out), .in1(comp_inst_1_comp_out), .out(multiplexer_2_out), .sel(and_1_out));
  Multiplexer #(.width(16), .enable("false")) multiplexer_3 (
    .in0(multiplexer_2_out), .in1(Op1), .out(OUT_ALU), .sel(comparator_1_eq));

  assign sel_op_alu[2] = sel_op_alu[3];
endmodule

module LSL_INST (
  input  [15:0] Op1,
  input  [3:0] sel_shift,
  input  [2:0] sel_op_shift,
  output [15:0] LSL_OUT
);

  wire [15:0] shifter_1_out, shifter_2_out, shifter_3_out, shifter_4_out;

  // Text text_1: pin names not known
  // Text text_2: pin names not known
  // Text text_3: pin names not known
  // Text text_4: pin names not known
  // Text text_5: pin names not known
  Shifter #(.width(16), .shift("ar")) shifter_1 (.in(Op1), .\dist (sel_shift), .out(shifter_1_out));
  Shifter #(.width(16)) shifter_2 (.in(Op1), .\dist (sel_shift), .out(shifter_2_out));
  Shifter #(.width(16), .shift("lr")) shifter_3 (.in(Op1), .\dist (sel_shift), .out(shifter_3_out));
  Shifter #(.width(16), .shift("rr")) shifter_4 (.in(Op1), .\dist (sel_shift), .out(shifter_4_out));
  Multiplexer #(.select(3), .width(16), .enable("false")) multiplexer_1 (
    .in0({16{1'b0}}), .in1(shifter_1_out), .in2(shifter_2_out), .in3(shifter_3_out), .in4(shifter_4_out),
    .in5({16{1'b0}}), .in6({16{1'b0}}), .in7({16{1'b0}}), .out(LSL_OUT), .sel(sel_op_shift));
endmodule

module ADD_INST (
  input  [15:0] Op1,
  input  [15:0] Op2,
  input  ACTIV,
  output [15:0] ADD_OUT
);

  wire [15:0] adder_1_out, demultiplexer_1_out0;

  // Text text_1: pin names not known
  // Text text_2: pin names not known
  // Text text_3: pin names not known
  // Text text_4: pin names not known
  // Text text_5: pin names not known
  Demultiplexer #(.width(16), .enable("false")) demultiplexer_1 (
    .out0(demultiplexer_1_out0), .out1(ADD_OUT), .in(adder_1_out), .sel(ACTIV));
  Adder #(.width(16)) adder_1 (.a(Op1), .b(Op2), .out(adder_1_out), .cin(1'b0));  // open: cout
  // also tied to GND on the sheet: {demultiplexer_1_out0[0], demultiplexer_1_out0[1], demultiplexer_1_out0[2], demultiplexer_1_out0[3], demultiplexer_1_out0[4], demultiplexer_1_out0[5], demultiplexer_1_out0[6], demultiplexer_1_out0[7], demultiplexer_1_out0[8], demultiplexer_1_out0[9], demultiplexer_1_out0[10], demultiplexer_1_out0[11], demultiplexer_1_out0[12], demultiplexer_1_out0[13], demultiplexer_1_out0[14], demultiplexer_1_out0[15]}
endmodule

module SUB_INST (
  input  [15:0] Op1,
  input  [15:0] Op2,
  input  ACTIV,
  output [15:0] SUB_OUT
);

  wire [15:0] demultiplexer_1_out0, subtractor_1_out;

  // Text text_1: pin names not known
  // Text text_2: pin names not known
  // Text text_3: pin names not known
  // Text text_4: pin names not known
  // Text text_5: pin names not known
  Demultiplexer #(.width(16), .enable("false")) demultiplexer_1 (
    .out0(demultiplexer_1_out0), .out1(SUB_OUT), .in(subtractor_1_out), .sel(ACTIV));
  Subtractor #(.width(16)) subtractor_1 (.a(Op1), .b(Op2), .out(subtractor_1_out), .bin(1'b0));  // open: bout
  // also tied to GND on the sheet: {demultiplexer_1_out0[0], demultiplexer_1_out0[1], demultiplexer_1_out0[2], demultiplexer_1_out0[3], demultiplexer_1_out0[4], demultiplexer_1_out0[5], demultiplexer_1_out0[6], demultiplexer_1_out0[7], demultiplexer_1_out0[8], demultiplexer_1_out0[9], demultiplexer_1_out0[10], demultiplexer_1_out0[11], demultiplexer_1_out0[12], demultiplexer_1_out0[13], demultiplexer_1_out0[14], demultiplexer_1_out0[15]}
endmodule
